# Fritzing sketch interrupt (saved by Fritzing 0.9.3b)
breadboards: 1

parts:
  パーツ1 = Arduino Uno (Rev3)
  R1 = Resistor [tolerance=±5% resistance=1k package="2512 [SMD]"]
  LED1 = RGB LED (com. cathode, rgb) [package="5 mm [THT]"]
  R2 = Resistor [tolerance=±5% resistance=1k package="2512 [SMD]"]
  R3 = Resistor [tolerance=±5% resistance=1k package="2512 [SMD]"]
  S1 = Pushbutton [package="[THT]"]
  R4 = Resistor [tolerance=±5% resistance=10k package="2512 [SMD]"]

nets:
  N1: パーツ1.GND, LED1.green_anode, R4.Pin_1
  N2: パーツ1.D2, S1.Pin_3, S1.Pin_4, R4.Pin_0
  N3: パーツ1.D5_PWM, R3.Pin_1
  N4: パーツ1.D6_PWM, R2.Pin_1
  N5: パーツ1.D7, R1.Pin_1
  N6: パーツ1.5V, S1.Pin_1, S1.Pin_2
  N7: R1.Pin_0, LED1.red_anode
  N8: LED1.common_cathode, R2.Pin_0
  N9: LED1.blue_anode, R3.Pin_0
